# Fritzing sketch Hardware Design Main (saved by Fritzing 0.9.3b)
breadboards: 2

parts:
  Part2 = Arduino Mega ADK (Rev3)
  DS8 = DS18B20 1-Wire Temperature Sensor [part_number=DS18B20]
  S17 = PH meter [package=THT]
  S18 = PH meter [package=THT]
  8_Channel_Relay2 = 8 Channel Power Relay
  Mod2 = Raspberry Pi 4B
  R9 = Resistor [tolerance=±5% resistance=10k package="2512 [SMD]"]
  R10 = Resistor [tolerance=±5% resistance=4.7k package="2512 [SMD]"]
  DHT5 = Humidity and Temperature Sensor DHT11
  LCD2 = LCD screen
  LCM1602_IIC1 = LCM1602 IIC [part_number="LCM1602 IIC" chip_label="LCM1602 IIC" package="DIP (Dual Inline) [THT]"]
  S21 = Round Pushbutton
  hc-sr1 = hc-sr04
  S22 = Round Pushbutton
  S23 = Round Pushbutton
  S24 = Round Pushbutton

nets:
  N1: Part2.A0, S18.pin1
  N2: Part2.A3, S17.pin1
  N3: Part2.D21/SCL, LCM1602_IIC1.SCL
  N4: Part2.D20/SDA, LCM1602_IIC1.SDA
  N5: Part2.D12_PWM, S21.leg0
  N6: Part2.D11_PWM, S23.leg0
  N7: Part2.D10_PWM, S22.leg0
  N8: Part2.D9_PWM, S24.leg0
  N9: Part2.D8_PWM, hc-sr1.Trig
  GND: Part2.D4_PWM, DS8.GND, S17.pin3, S18.pin3, hc-sr1.GND, S24.leg1
  N10: Part2.D6_PWM, hc-sr1.Echo
  N11: DS8.DQ, R10.Pin_0
  VDD: DS8.VDD, S17.pin2, S18.pin2, R10.Pin_1, hc-sr1.VCC
  GND_2: 8_Channel_Relay2.GND, Mod2.GND, DHT5.GND_2
  N12: 8_Channel_Relay2.IN1, Mod2.GPIO18
  N13: 8_Channel_Relay2.IN2, Mod2.GPIO22
  N14: 8_Channel_Relay2.IN3, Mod2.GPIO24
  N15: 8_Channel_Relay2.IN4, Mod2.GPIO25
  N16: 8_Channel_Relay2.IN5, Mod2.GPIO5
  N17: 8_Channel_Relay2.IN6, Mod2.GPIO16
  VCC: 8_Channel_Relay2.VCC, Mod2.5V
  3V3: Mod2.3V3, R9.Pin_0, DHT5.Vcc
  N18: Mod2.GPIO17, R9.Pin_1, DHT5.Data-signal
  VSS: LCD2.VSS, LCM1602_IIC1.VSS
  VDD_2: LCD2.VDD, LCM1602_IIC1.VDD
  N19: LCD2.V0, LCM1602_IIC1.V0
  N20: LCD2.RS, LCM1602_IIC1.RS
  N21: LCD2.R/W, LCM1602_IIC1.RW
  N22: LCD2.E, LCM1602_IIC1.E
  N23: LCD2.DB0, LCM1602_IIC1.D0
  N24: LCD2.DB1, LCM1602_IIC1.D1
  N25: LCD2.DB2, LCM1602_IIC1.D2
  N26: LCD2.DB3, LCM1602_IIC1.D3
  N27: LCD2.DB4, LCM1602_IIC1.D4
  N28: LCD2.DB5, LCM1602_IIC1.D5
  N29: LCD2.DB6, LCM1602_IIC1.D6
  N30: LCD2.DB7, LCM1602_IIC1.D7
  N31: LCD2.LED+, LCM1602_IIC1.A
  N32: LCD2.LED-, LCM1602_IIC1.K

notes:
  Spare 3 (GPIO 18, In 1)
  Spare 2 (GPIO 22, In 2)
  Spare 1(GPIO 24, In 3)
  Light (GPIO 25, In 4)
  Pump (GPIO 5, In 5)
  Fan (GPIO 16, In 6)
  Sensor Temperature dan Humidity Ruangan
  TDS Sensor (A0)
  pH Sensor (A3)

custom parts:
  8 Channel Power Relay: An 8 channel power relay. The module operates at 5V.
  Humidity and Temperature Sensor DHT11: Digital relative humidity & temperature sensor DHT11
  LCM1602 IIC: I2C-Module to use a 1602 or 2004 LCD on with the wire.h libory Serial LCD Modul
